// Digital circuit ex2-1.dig as structural Verilog
module ex2_1 (
  input  [9:0] IN,
  output OUT
);

  and and_1 (OUT, IN[0], IN[9]);
endmodule

/* Test case EX2-1 Test:
IN OUT 

# Positive Even
 0b0101011000 0
 0b0110000100 0

# Positive Odd
 0b0110010111 0
 0b0111111111 0

# Negative Even
 0b1001000110 0
 0b1010001110 0

# Negative Odd
 0b1011101101 1
 0b1110011001 1
*/
