// Digital circuit Lab02.dig as structural Verilog
module Lab02 (
  input  B,
  input  C,
  input  A,
  input  D,
  output Fa,
  output Fb,
  output Fc,
  output Fd,
  output Fe,
  output Fg,
  output Ff
);

  wire A_t, and_1_out, and_2_out, and_3_out, and_4_out, and_5_out, and_6_out, and_7_out, and_8_out,
       and_9_out, and_10_out, and_11_out, and_12_out, and_13_out, and_14_out, and_15_out, and_16_out,
       and_17_out, and_18_out, and_19_out, and_20_out, and_21_out, and_22_out, and_23_out, and_24_out,
       and_25_out, and_26_out, and_27_out, and_28_out, and_29_out, and_30_out, and_31_out, and_32_out,
       and_33_out, and_34_out, and_35_out, B_t, C_t, D_t, or_1_out, or_2_out, or_3_out, or_4_out, or_5_out,
       or_6_out, or_7_out, or_8_out, or_9_out, or_10_out, or_11_out, or_12_out, or_13_out, or_14_out,
       or_15_out;

  not not_1 (A_t, A);
  not not_2 (B_t, B);
  not not_3 (C_t, C);
  not not_4 (D_t, D);
  and and_1 (and_1_out, B_t, D_t);
  and and_2 (and_2_out, C, D_t);
  and and_3 (and_3_out, A_t, C);
  and and_4 (and_4_out, A_t, B, D);
  and and_5 (and_5_out, A, B_t, C_t);
  and and_6 (and_6_out, A, B, C);
  and and_7 (and_7_out, A_t, B_t);
  and and_8 (and_8_out, B_t, D_t);
  and and_9 (and_9_out, A, D, C_t);
  and and_10 (and_10_out, A_t, C, D);
  and and_11 (and_11_out, A_t, C_t, D_t);
  and and_12 (and_12_out, A, B_t);
  and and_13 (and_13_out, A_t, B);
  and and_14 (and_14_out, A_t, D);
  and and_15 (and_15_out, D, C_t);
  and and_16 (and_16_out, A_t, C_t);
  and and_17 (and_17_out, A, C_t);
  and and_18 (and_18_out, B, C, D_t);
  and and_19 (and_19_out, B, D, C_t);
  and and_20 (and_20_out, B_t, C, D);
  and and_21 (and_21_out, A_t, B_t, D_t);
  and and_22 (and_22_out, A, B);
  and and_23 (and_23_out, A, C);
  and and_24 (and_24_out, C, D_t);
  and and_25 (and_25_out, B_t, D_t);
  and and_26 (and_26_out, A, C);
  and and_27 (and_27_out, A, B_t);
  and and_28 (and_28_out, A_t, B, C_t);
  and and_29 (and_29_out, B, D_t);
  and and_30 (and_30_out, C_t, D_t);
  and and_31 (and_31_out, A, D);
  and and_32 (and_32_out, A, B_t);
  and and_33 (and_33_out, A_t, B, C_t);
  and and_34 (and_34_out, B_t, C);
  and and_35 (and_35_out, C, D_t);
  or or_1 (or_1_out, and_1_out, and_2_out);
  or or_2 (or_2_out, and_3_out, and_4_out);
  or or_3 (or_3_out, and_5_out, and_6_out);
  or or_4 (or_4_out, and_7_out, and_8_out);
  or or_5 (or_5_out, and_10_out, and_11_out);
  or or_6 (or_6_out, and_12_out, and_13_out);
  or or_7 (or_7_out, and_14_out, and_15_out);
  or or_8 (or_8_out, and_18_out, and_19_out);
  or or_9 (or_9_out, and_20_out, and_21_out);
  or or_10 (or_10_out, and_22_out, and_23_out);
  or or_11 (or_11_out, and_24_out, and_25_out);
  or or_12 (or_12_out, and_26_out, and_27_out);
  or or_13 (or_13_out, and_29_out, and_30_out);
  or or_14 (or_14_out, and_31_out, and_32_out);
  or or_15 (or_15_out, and_34_out, and_35_out);
  or or_16 (Fe, or_10_out, or_11_out);
  or or_17 (Ff, or_12_out, and_28_out, or_13_out);
  or or_18 (Fg, or_14_out, and_33_out, or_15_out);
  or or_19 (Fa, or_1_out, or_2_out, or_3_out);
  or or_20 (Fb, or_4_out, and_9_out, or_5_out);
  or or_21 (Fc, or_6_out, or_7_out, and_16_out);
  or or_22 (Fd, and_17_out, or_8_out, or_9_out);
  Seven_Seg seven_seg_1 (.a(Fa), .b(Fb), .c(Fc), .d(Fd), .e(Fe), .f(Ff), .g(Fg), .dp(1'b0));
endmodule
