// Digital circuit register-file.dig as structural Verilog
module register_file (
  input  [4:0] ReadReg1,
  input  [4:0] ReadReg2,
  input  [31:0] WriteReg,
  input  [31:0] WriteData,
  input  RegWrite,
  input  Clock,
  output [31:0] ReadData1,
  output [31:0] ReadData2
);

  wire and_1_out, and_2_out, and_3_out, and_4_out, and_5_out, and_6_out, and_7_out, and_8_out, and_9_out,
       and_10_out, and_11_out, and_12_out, and_13_out, and_14_out, and_15_out, and_16_out, and_17_out,
       and_18_out, and_19_out, and_20_out, and_21_out, and_22_out, and_23_out, and_24_out, and_25_out,
       and_26_out, and_27_out, and_28_out, and_29_out, and_30_out, and_31_out, DC0, DC1, DC2, DC3, DC4, DC5,
       DC6, DC7, DC8, DC9, DC10, DC11, DC12, DC13, DC14, DC15, DC16, DC17, DC18, DC19, DC20, DC21, DC22,
       DC23, DC24, DC25, DC26, DC27, DC28, DC29, DC30, DC31;
  wire [31:0] REG1, REG2, REG3, REG4, REG5, REG6, REG7, REG8, REG9, REG10, REG11, REG12, REG13, REG14, REG15,
       REG16, REG17, REG18, REG19, REG20, REG21, REG22, REG23, REG24, REG25, REG26, REG27, REG28, REG29,
       REG30, REG31;

  Decoder #(.Selector_Bits(5)) decoder_1 (
    .sel(WriteReg[4:0]), .out_0(DC0), .out_1(DC1), .out_2(DC2), .out_3(DC3), .out_4(DC4), .out_5(DC5),
    .out_6(DC6), .out_7(DC7), .out_8(DC8), .out_9(DC9), .out_10(DC10), .out_11(DC11), .out_12(DC12),
    .out_13(DC13), .out_14(DC14), .out_15(DC15), .out_16(DC16), .out_17(DC17), .out_18(DC18), .out_19(DC19),
    .out_20(DC20), .out_21(DC21), .out_22(DC22), .out_23(DC23), .out_24(DC24), .out_25(DC25), .out_26(DC26),
    .out_27(DC27), .out_28(DC28), .out_29(DC29), .out_30(DC30), .out_31(DC31));
  and and_1 (and_1_out, DC9, RegWrite);
  and and_2 (and_2_out, DC10, RegWrite);
  and and_3 (and_3_out, DC11, RegWrite);
  and and_4 (and_4_out, DC12, RegWrite);
  and and_5 (and_5_out, DC13, RegWrite);
  and and_6 (and_6_out, DC14, RegWrite);
  and and_7 (and_7_out, DC15, RegWrite);
  and and_8 (and_8_out, DC16, RegWrite);
  and and_9 (and_9_out, DC17, RegWrite);
  and and_10 (and_10_out, DC18, RegWrite);
  and and_11 (and_11_out, DC19, RegWrite);
  and and_12 (and_12_out, DC20, RegWrite);
  and and_13 (and_13_out, DC21, RegWrite);
  and and_14 (and_14_out, DC22, RegWrite);
  and and_15 (and_15_out, DC23, RegWrite);
  and and_16 (and_16_out, DC24, RegWrite);
  and and_17 (and_17_out, DC25, RegWrite);
  and and_18 (and_18_out, DC26, RegWrite);
  and and_19 (and_19_out, DC27, RegWrite);
  and and_20 (and_20_out, DC28, RegWrite);
  and and_21 (and_21_out, DC29, RegWrite);
  and and_22 (and_22_out, DC30, RegWrite);
  and and_23 (and_23_out, DC31, RegWrite);
  and and_24 (and_24_out, DC1, RegWrite);
  and and_25 (and_25_out, DC2, RegWrite);
  and and_26 (and_26_out, DC3, RegWrite);
  and and_27 (and_27_out, DC4, RegWrite);
  and and_28 (and_28_out, DC5, RegWrite);
  and and_29 (and_29_out, DC6, RegWrite);
  and and_30 (and_30_out, DC7, RegWrite);
  and and_31 (and_31_out, DC8, RegWrite);
  Register #(.Bits(32)) register_1 (.D(WriteReg), .C(Clock), .en(and_21_out), .Q(REG29));
  Register #(.Bits(32)) register_2 (.D(WriteReg), .C(Clock), .en(and_22_out), .Q(REG30));
  Register #(.Bits(32)) register_3 (.D(WriteReg), .C(Clock), .en(and_23_out), .Q(REG31));
  Register #(.Bits(32)) register_4 (.D(WriteReg), .C(Clock), .en(and_24_out), .Q(REG1));
  Register #(.Bits(32)) register_5 (.D(WriteReg), .C(Clock), .en(and_25_out), .Q(REG2));
  Register #(.Bits(32)) register_6 (.D(WriteReg), .C(Clock), .en(and_26_out), .Q(REG3));
  Register #(.Bits(32)) register_7 (.D(WriteReg), .C(Clock), .en(and_27_out), .Q(REG4));
  Register #(.Bits(32)) register_8 (.D(WriteReg), .C(Clock), .en(and_28_out), .Q(REG5));
  Register #(.Bits(32)) register_9 (.D(WriteReg), .C(Clock), .en(and_29_out), .Q(REG6));
  Register #(.Bits(32)) register_10 (.D(WriteReg), .C(Clock), .en(and_30_out), .Q(REG7));
  Register #(.Bits(32)) register_11 (.D(WriteReg), .C(Clock), .en(and_31_out), .Q(REG8));
  Register #(.Bits(32)) register_12 (.D(WriteReg), .C(Clock), .en(and_1_out), .Q(REG9));
  Register #(.Bits(32)) register_13 (.D(WriteReg), .C(Clock), .en(and_2_out), .Q(REG10));
  Register #(.Bits(32)) register_14 (.D(WriteReg), .C(Clock), .en(and_3_out), .Q(REG11));
  Register #(.Bits(32)) register_15 (.D(WriteReg), .C(Clock), .en(and_4_out), .Q(REG12));
  Register #(.Bits(32)) register_16 (.D(WriteReg), .C(Clock), .en(and_5_out), .Q(REG13));
  Register #(.Bits(32)) register_17 (.D(WriteReg), .C(Clock), .en(and_6_out), .Q(REG14));
  Register #(.Bits(32)) register_18 (.D(WriteReg), .C(Clock), .en(and_7_out), .Q(REG15));
  Register #(.Bits(32)) register_19 (.D(WriteReg), .C(Clock), .en(and_8_out), .Q(REG16));
  Register #(.Bits(32)) register_20 (.D(WriteReg), .C(Clock), .en(and_9_out), .Q(REG17));
  Register #(.Bits(32)) register_21 (.D(WriteReg), .C(Clock), .en(and_10_out), .Q(REG18));
  Register #(.Bits(32)) register_22 (.D(WriteReg), .C(Clock), .en(and_11_out), .Q(REG19));
  Register #(.Bits(32)) register_23 (.D(WriteReg), .C(Clock), .en(and_12_out), .Q(REG20));
  Register #(.Bits(32)) register_24 (.D(WriteReg), .C(Clock), .en(and_13_out), .Q(REG21));
  Register #(.Bits(32)) register_25 (.D(WriteReg), .C(Clock), .en(and_14_out), .Q(REG22));
  Register #(.Bits(32)) register_26 (.D(WriteReg), .C(Clock), .en(and_15_out), .Q(REG23));
  Register #(.Bits(32)) register_27 (.D(WriteReg), .C(Clock), .en(and_16_out), .Q(REG24));
  Register #(.Bits(32)) register_28 (.D(WriteReg), .C(Clock), .en(and_17_out), .Q(REG25));
  Register #(.Bits(32)) register_29 (.D(WriteReg), .C(Clock), .en(and_18_out), .Q(REG26));
  Register #(.Bits(32)) register_30 (.D(WriteReg), .C(Clock), .en(and_19_out), .Q(REG27));
  Register #(.Bits(32)) register_31 (.D(WriteReg), .C(Clock), .en(and_20_out), .Q(REG28));
  Multiplexer #(.Bits(32), .Selector_Bits(5)) multiplexer_1 (
    .sel(ReadReg1), .in_0({32{1'b0}}), .in_1(REG1), .in_2(REG2), .in_3(REG3), .in_4(REG4), .in_5(REG5),
    .in_6(REG6), .in_7(REG7), .in_8(REG8), .in_9(REG9), .in_10(REG10), .in_11(REG11), .in_12(REG12),
    .in_13(REG13), .in_14(REG14), .in_15(REG15), .in_16(REG16), .in_17(REG17), .in_18(REG18), .in_19(REG19),
    .in_20(REG20), .in_21(REG21), .in_22(REG22), .in_23(REG23), .in_24(REG24), .in_25(REG25), .in_26(REG26),
    .in_27(REG27), .in_28(REG28), .in_29(REG29), .in_30(REG30), .in_31(REG31), .out(ReadData1));
  Multiplexer #(.Selector_Bits(5), .Bits(32)) multiplexer_2 (
    .sel(ReadReg2), .in_0({32{1'b0}}), .in_1(REG1), .in_2(REG2), .in_3(REG3), .in_4(REG4), .in_5(REG5),
    .in_6(REG6), .in_7(REG7), .in_8(REG8), .in_9(REG9), .in_10(REG10), .in_11(REG11), .in_12(REG12),
    .in_13(REG13), .in_14(REG14), .in_15(REG15), .in_16(REG16), .in_17(REG17), .in_18(REG18), .in_19(REG19),
    .in_20(REG20), .in_21(REG21), .in_22(REG22), .in_23(REG23), .in_24(REG24), .in_25(REG25), .in_26(REG26),
    .in_27(REG27), .in_28(REG28), .in_29(REG29), .in_30(REG30), .in_31(REG31), .out(ReadData2));
  // Pins of 5 and 32 bits meet at WriteReg

  // Other names for the same wires on the sheet: C = Clock; RD1[31:0] = ReadData1; RD2[31:0] = ReadData2;
  //   RR1[4:0] = ReadReg1; RR2[4:0] = ReadReg2; RW = RegWrite; WD[31:0] = WriteData; WR[31:0] = WriteReg
endmodule

/* Test case Register File Test:
WriteReg WriteData RegWrite Clock ReadReg1 ReadReg2 ReadData1 ReadData2

# $1 = 25
1 25 1 C 1 0 25 0

# $2 = 30
2 30 1 C 0 2 0 30

# $(N+1) = (N+1)
loop(N, 30)
	(N+1) (N+1) 1 C (N+1) (N) (N+1) (N)
end loop

# $(N+1) = N-60
loop(N, 30)
	(N+1) (N-60) 1 C (N+1) (N+1) (N-60) (N-60)
end loop

# Try writing to $0. This should not write anything
0 25 1 C 0 0 0 0

# try writing when RegWrite = 0
# (the registers should still have their old values)
loop(N, 30)
	(N+1) (N+80) 0 C (N+1) (N+1) (N-60) (N-60)
end loop
*/
